# Fritzing sketch Schematic (saved by Fritzing 0.9.9b)
circuit board: 8.46667cm x 5.64444cm
breadboards: 2

parts:
  Part1 = Arduino Nano (Rev3.0)
  R1 = Resistor [tolerance=±5% power=0.25 resistance=220 package=THT]
  S1 = SWITCH-MOMENTARY-2 [package=tactile-switch-1101ne]
  R2 = Resistor [tolerance=±5% power=0.25 resistance=220 package=THT]
  R3 = Resistor [tolerance=±5% power=0.25 resistance=220 package=THT]
  S2 = SWITCH-MOMENTARY-2 [package=tactile-switch-1101ne]
  S3 = SWITCH-MOMENTARY-2 [package=tactile-switch-1101ne]
  J1 = Piezo Speaker
  Part2 = Bluetooth HC-05 Macho
  R4 = Resistor [tolerance=±5% power=0.25 resistance=220 package=THT]
  R5 = Resistor [tolerance=±5% power=0.25 resistance=220 package=THT]
  LCD1 = LCD screen
  R6 = Resistor [tolerance=±5% power=0.25 resistance=220 package=THT]
  U1 = POT [package=pot_mammoth]  # not connected

nets (from the schematic view):
  GND: Part1.GND, R1.Pin_1, R2.Pin_1, R3.Pin_1, J1.pin2, Part2.GND, LCD1.LED-
  N1: Part1.D2, R4.Pin_0
  N2: Part1.D3, Part2.RXD
  N3: Part1.D4, J1.pin1
  N4: Part1.D5, R3.Pin_0, S3.1
  N5: Part1.D6, R2.Pin_0, S2.1
  N6: Part1.D7, R1.Pin_0, S1.1
  N7: Part1.D8, LCD1.DB4
  N8: Part1.D9, LCD1.DB3
  N9: Part1.D10, LCD1.DB2
  N10: Part1.D11/MOSI, LCD1.DB1
  N11: Part2.TXD, R4.Pin_1, R5.Pin_0
  N12: LCD1.LED+, R6.Pin_1
